// Logisim project Exercicio 1 - segunda folha.circ as structural Verilog: 1 circuit, main circuit main
module main (
  input  A,
  input  B,
  input  C,
  input  D,
  input  E
);

  wire S1_out, S2_out, S_out;

  or S1 (S1_out, A, B, C);
  or S2 (S2_out, D, E);
  nand S (S_out, S1_out, S2_out);
  LED led_1 (.in(S_out));

  // Notes on the sheet:
  //   S = !( S1 * S2 )
endmodule
