// Logisim project Exercicio 1.circ as structural Verilog: 1 circuit, main circuit main
module main (
  input  A,
  input  B,
  input  C,
  input  D,
  input  E
);

  wire and_1_out, and_2_out, and_3_out;

  and and_1 (and_1_out, A, B, C);
  and and_2 (and_2_out, D, E);
  and and_3 (and_3_out, and_1_out, and_2_out);
  LED led_1 (.in(and_3_out));

  // Notes on the sheet:
  //   S = S1 * S2
endmodule
