// Logisim project Exercicio 2 - segunda folha.circ as structural Verilog: 1 circuit, main circuit main
module main (
  input  A,
  input  B,
  input  C,
  input  D,
  input  E,
  input  F
);

  wire S1_out, S2_out, S3_out, S4_out, S_out;

  or S1 (S1_out, B, D);
  and S2 (S2_out, E, F);
  and S3 (S3_out, A, S1_out);
  or S4 (S4_out, C, S2_out);
  or S (S_out, S3_out, S4_out);
  LED led_1 (.in(S_out));

  // Notes on the sheet:
  //   S = A( B+D ) + (E * F) + C
endmodule
