// Logisim project Exercicio 2.circ as structural Verilog: 1 circuit, main circuit main
module main (
  input  A,
  input  B,
  input  C,
  input  D,
  input  E,
  input  F
);

  wire and_1_out, and_2_out, or_1_out, or_2_out;

  and and_1 (and_1_out, A, C);
  or or_1 (or_1_out, B, D);
  and and_2 (and_2_out, E, E);
  or or_2 (or_2_out, and_1_out, or_1_out, and_2_out);
  LED led_1 (.in(or_2_out));

  assign F = E;

  // Notes on the sheet:
  //   S = (AC) + (B+D) + (EF)
endmodule
