// Logisim project Exercicio 3.circ as structural Verilog: 1 circuit, main circuit main
module main (
  input  A,
  input  B,
  input  C,
  input  D
);

  wire and_1_out, and_2_out, and_3_out, not_1_out, not_2_out, not_3_out, not_4_out, not_5_out, not_6_out,
       or_1_out;

  not not_1 (not_1_out, A);
  not not_2 (not_2_out, C);
  not not_3 (not_3_out, B);
  not not_4 (not_4_out, C);
  not not_5 (not_5_out, D);
  not not_6 (not_6_out, B);
  and and_1 (and_1_out, not_1_out, B, not_2_out, D);
  and and_2 (and_2_out, A, not_3_out, not_4_out, not_5_out);
  and and_3 (and_3_out, A, not_6_out, C, D);
  or or_1 (or_1_out, and_1_out, and_2_out, and_3_out);
  LED led_1 (.in(or_1_out));

  // Notes on the sheet:
  //   S = ( !A * B * !C * D ) + ( A * !B * !C * !D ) + ( A * !B * C * D )
endmodule
