// Logisim project Exercicio 1.circ as structural Verilog: 1 circuit, main circuit main
module main (
  input  A,
  input  B,
  input  C,
  input  D,
  input  E,
  output out_6
);

  wire S1_out, S2_out;

  and S1 (S1_out, A, B, C);
  and S2 (S2_out, D, E);
  or S (out_6, S1_out, S2_out);

  // Notes on the sheet:
  //   S = S1 + S2
endmodule
