// Logisim project Exercicio 2.circ as structural Verilog: 1 circuit, main circuit main
module main (
  input  A,
  input  B,
  input  C,
  input  D,
  input  E,
  input  F,
  output out_7
);

  wire S1_out, S2_out, S3_out;

  and S1 (S1_out, A, B);
  and S2 (S2_out, C, D);
  and S3 (S3_out, E, F);
  or S (out_7, S1_out, S2_out, S3_out);

  // Notes on the sheet:
  //   S = S1 + S2 = S3
endmodule
